# Fritzing sketch watering (saved by Fritzing 0.9.9b)
circuit board: 8.46667cm x 5.64444cm
breadboards: 1

parts:
  WeMos_D1_Mini1 = WeMos D1 Mini
  water_tank_level_sensor = HC-SR04 Ultrasonic Distance Sensor
  pump_relay = KY-019 5V Relay Module [package="Breakout board"]
  Bauteil2 = FC-28 Soil Hygrometer Module
  soil_sensor1 = FC-28 Soil Hygrometer Module - Probe
  PUMP = DC Motor
  J1 = Power Jack [package=power_jack_pth]
  V1 = DC Power [voltage=5]
  Bauteil3 = Arduino Nano (Rev3.0)
  Bauteil4 = FC-28 Soil Hygrometer Module
  soil_sensor0 = FC-28 Soil Hygrometer Module - Probe

nets:
  VCC: WeMos_D1_Mini1.5V, water_tank_level_sensor.VCC, pump_relay.+, Bauteil2.VCC, J1.PWR, Bauteil3.VIN, Bauteil4.VCC
  N1: WeMos_D1_Mini1.D4, pump_relay.S
  GND: WeMos_D1_Mini1.G, water_tank_level_sensor.GND, pump_relay.-, Bauteil2.GND, PUMP.pin_2, J1.GND, V1.V-, Bauteil3.GND, Bauteil4.GND
  N2: water_tank_level_sensor.TRIG, Bauteil3.D12/MISO
  N3: water_tank_level_sensor.ECHO, Bauteil3.D11/MOSI
  N4: pump_relay.Common, PUMP.pin_1
  N5: Bauteil2.AO, Bauteil3.A1
  N6: Bauteil2.POS, soil_sensor1.POS
  N7: Bauteil2.NEG, soil_sensor1.NEG
  N8: Bauteil3.A0, Bauteil4.AO
  N9: Bauteil4.POS, soil_sensor0.POS
  N10: Bauteil4.NEG, soil_sensor0.NEG

custom parts:
  KY-019 5V Relay Module: KY-019 5V Relay module, used to control AC circuits. (Special thanks to vanepp for fixing the PCB holes and other errors)
  FC-28 Soil Hygrometer Module: The FC-28 is a soil hygrometer module that uses the Texas Instruments LM393 comparator chip to provide an analog measurement of soil humidity. The digital output is high when soil moisture is over a certain threshold, as determined by adjusting the potentiometer.
  FC-28 Soil Hygrometer Module - Probe: The FC-28 is a soil hygrometer module that uses the Texas Instruments LM393 comparator chip to provide an analog measurement of soil humidity.
